// Logisim project cpu.circ as structural Verilog: 9 circuits, main circuit NPC
module main (
  input  reset,
  output [31:0] out_2,
  output out_3,
  output [4:0] out_4,
  output [31:0] out_5,
  output out_6,
  output [4:0] out_7,
  output [31:0] out_8
);

  wire controller_1_alusrc, controller_1_branch, controller_1_extop, controller_1_memtor,
       controller_1_regdst, jump, zero;
  wire [1:0] controller_1_aluop;
  wire [31:0] dm_1_readdata, ext_1_out_3, grf_1_rd1, MemAdder, multiplexer_3_out, npc_1_npc, pc_1_out_2;

  Clock clock_1 (.out(reset));
  NPC npc_1 (
    .PC(pc_1_out_2), .imm(out_2[15:0]), .imm26(out_2[25:0]), .zero(zero), .Branch(controller_1_branch),
    .jump(jump), .npc(npc_1_npc));
  PC pc_1 (.NPC(npc_1_npc), .out_2(pc_1_out_2));
  IM im_1 (.PC(pc_1_out_2), .instr(out_2));
  Controller controller_1 (
    .op(out_2[31:26]), .fn(out_2[5:0]), .aluop(controller_1_aluop), .regDst(controller_1_regdst),
    .aluSrc(controller_1_alusrc), .memToR(controller_1_memtor), .memWrite(out_6), .regWrite(out_3),
    .extOp(controller_1_extop), .jumpOp(jump), .branch(controller_1_branch));
  Multiplexer #(.width(32), .enable("false")) multiplexer_1 (
    .in0({MemAdder[31:7], out_7, MemAdder[1:0]}), .in1(dm_1_readdata), .out(out_5), .sel(controller_1_memtor));
  Multiplexer #(.width(5), .enable("false")) multiplexer_2 (
    .in0(out_2[20:16]), .in1(out_2[15:11]), .out(out_4), .sel(controller_1_regdst));
  EXT ext_1 (.in_1(out_2[15:0]), .extop(controller_1_extop), .out_3(ext_1_out_3));
  GRF grf_1 (
    .A1(out_2[25:21]), .A2(out_2[20:16]), .A3(out_4), .WD(out_5), .clk(reset), .reset(reset), .we(out_3),
    .RD1(grf_1_rd1), .RD2(out_8));
  ALU alu_1 (
    .in_1(controller_1_aluop), .rd1(grf_1_rd1), .rd2(multiplexer_3_out),
    .result({MemAdder[31:7], out_7, MemAdder[1:0]}), .out_5(zero));
  Multiplexer #(.width(32), .enable("false")) multiplexer_3 (
    .in0(out_8), .in1(ext_1_out_3), .out(multiplexer_3_out), .sel(controller_1_alusrc));
  DM dm_1 (.A(out_7), .WD(out_8), .Clk(reset), .WE(out_6), .in_5(reset), .ReadData(dm_1_readdata));

  // Other names for the same wires on the sheet: clk = reset; est[15:0] = out_2[15:0]; Instr[31:0] = out_2;
  //   MemAdder[6:2] = out_7; MemData[31:0] = out_8; MemWrite = out_6; RedAdder[4:0] = out_4; RedWrite = out_3;
  //   RegData[31:0] = out_5
endmodule

module NPC (
  input  [31:0] PC,
  input  [15:0] imm,
  input  jump,
  input  [25:0] imm26,
  input  zero,
  input  Branch,
  output [31:0] npc
);

  wire and_1_out;
  wire [31:0] adder_1_out, adder_2_out, bit_extender_1_out, multiplexer_1_out, shifter_1_out;

  assign bit_extender_1_out = {{16{imm[15]}}, imm};  // Bit_Extender bit_extender_1
  Shifter #(.width(32)) shifter_1 (.in(bit_extender_1_out), .\dist (5'b00010), .out(shifter_1_out));
  Adder #(.width(32)) adder_1 (.a(adder_2_out), .b(shifter_1_out), .out(adder_1_out));  // open: cin, cout
  Adder #(.width(32)) adder_2 (.a(PC), .b(32'h4), .out(adder_2_out));  // open: cin, cout
  Multiplexer #(.width(32), .enable("false")) multiplexer_1 (
    .in0(adder_2_out), .in1(adder_1_out), .out(multiplexer_1_out), .sel(and_1_out));
  and and_1 (and_1_out, zero, Branch);
  Multiplexer #(.width(32), .enable("false")) multiplexer_2 (
    .in0(multiplexer_1_out), .in1({PC[31:28], imm26, 2'b00}), .out(npc), .sel(jump));
endmodule

module IM (
  input  [31:0] PC,
  output [31:0] instr
);

  wire [31:0] subtractor_1_out;

  Subtractor #(.width(32)) subtractor_1 (.a(PC), .b(32'h3000), .out(subtractor_1_out));  // open: bin, bout
  ROM #(.addrWidth(5), .dataWidth(32)) rom_1 (.addr(subtractor_1_out[6:2]), .data(instr));  // open: sel

  // Notes on the sheet:
  //   contents of rom_1 (hex, n*v repeats v):
  //   3401007b 340201c8 221821 ac030000
endmodule

module EXT (
  input  [15:0] in_1,
  input  extop,
  output [31:0] out_3
);

  wire [31:0] bit_extender_1_out, bit_extender_2_out;

  assign bit_extender_1_out = {{16{1'b0}}, in_1};  // Bit_Extender bit_extender_1
  assign bit_extender_2_out = {{16{in_1[15]}}, in_1};  // Bit_Extender bit_extender_2
  Multiplexer #(.width(32), .enable("false")) multiplexer_1 (
    .in0(bit_extender_1_out), .in1(bit_extender_2_out), .out(out_3), .sel(extop));
endmodule

module ALU (
  input  [1:0] in_1,
  input  [31:0] rd1,
  input  [31:0] rd2,
  output [31:0] result,
  output out_5
);

  wire [31:0] adder_1_out, multiplexer_1_out, not_1_out, or_1_out;

  assign not_1_out = ~rd2;  // NOT_Gate not_1, 32 bits wide
  Multiplexer #(.width(32), .enable("false")) multiplexer_1 (
    .in0(rd2), .in1(not_1_out), .out(multiplexer_1_out), .sel(in_1[0]));
  Adder #(.width(32)) adder_1 (.a(rd1), .b(multiplexer_1_out), .out(adder_1_out), .cin(in_1[0]));  // open: cout
  assign or_1_out = rd1 | rd2;  // OR_Gate or_1, 32 bits wide
  Multiplexer #(.width(32), .enable("false")) multiplexer_2 (
    .in0(adder_1_out), .in1(or_1_out), .out(result), .sel(in_1[1]));
  Comparator #(.width(32)) comparator_1 (.a(result), .b({32{1'b0}}), .eq(out_5));  // open: gt, lt

  // Other names for the same wires on the sheet: cin = in_1[0]; m1 = in_1[0]; M2 = in_1[1]
endmodule

module DM (
  input  [4:0] A,
  input  [31:0] WD,
  input  Clk,
  input  WE,
  input  in_5,
  output [31:0] ReadData
);

  RAM #(.addrWidth(5), .dataWidth(32), .bus("separate")) ram_1 (
    .addr(A), .din(WD), .data(ReadData), .str(WE), .sel(1'b1), .clk(Clk), .ld(1'b1), .clr(in_5));
endmodule

module Controller (
  input  [5:0] op,
  input  [5:0] fn,
  output [1:0] aluop,
  output extOp,
  output memToR,
  output branch,
  output regDst,
  output aluSrc,
  output memWrite,
  output regWrite,
  output jumpOp
);

  wire add, sub, sw;

  buf or_1 (regDst, add);  // OR_Gate
  buf or_2 (aluSrc, aluop[1]);  // OR_Gate
  and and_1 (add, ~op[0], ~op[1], ~op[2], ~op[3], ~op[4], ~op[5], fn[0], ~fn[1], ~fn[2], ~fn[3], ~fn[4], fn[5]);  // AND_Gate
  and and_2 (sub, ~op[0], ~op[1], ~op[2], ~op[3], ~op[4], ~op[5], fn[0], ~fn[1], ~fn[2], ~fn[3], fn[4], fn[5]);  // AND_Gate
  buf or_3 (memWrite, sw);  // OR_Gate
  and and_3 (aluop[1], ~op[0], ~op[1], op[2], op[3], ~op[4], op[5]);  // AND_Gate
  and and_4 (memToR, op[0], ~op[1], ~op[2], ~op[3], op[4], op[5]);  // AND_Gate
  buf or_4 (regWrite, add);  // OR_Gate
  buf or_5 (extOp, memToR);  // OR_Gate
  and and_5 (sw, op[0], ~op[1], op[2], ~op[3], op[4], op[5]);  // AND_Gate
  and and_6 (branch, ~op[0], ~op[1], ~op[2], op[3], ~op[4], ~op[5]);  // AND_Gate
  or or_6 (aluop[0], sub, branch);
  and and_7 (jumpOp, ~op[0], ~op[1], ~op[2], ~op[3], op[4], ~op[5]);  // AND_Gate

  // Other names for the same wires on the sheet: ori = aluop[1]; beq = branch; j = jumpOp; lw = memToR
endmodule

module GRF (
  input  [4:0] A1,
  input  clk,
  input  reset,
  input  we,
  input  [4:0] A2,
  input  [4:0] A3,
  input  [31:0] WD,
  output [31:0] RD1,
  output [31:0] RD2
);

  wire [31:0] I0, I1, I2, I3, I4, I5, I6, I7, I8, I9, I10, I11, I12, I13, I14, I15, I16, I17, I18, I19, I20,
       I21, I22, I23, I24, I25, I26, I27, I28, I29, I30, I31, O0, O1, O2, O3, O4, O5, O6, O7, O8, O9, O10,
       O11, O12, O13, O14, O15, O16, O17, O18, O19, O20, O21, O22, O23, O24, O25, O26, O27, O28, O29, O30,
       O31;

  Demultiplexer #(.select(5), .width(32), .tristate("true")) demultiplexer_1 (
    .out0(I0), .out1(I1), .out2(I2), .out3(I3), .out4(I4), .out5(I5), .out6(I6), .out7(I7), .out8(I8),
    .out9(I9), .out10(I10), .out11(I11), .out12(I12), .out13(I13), .out14(I14), .out15(I15), .out16(I16),
    .out17(I17), .out18(I18), .out19(I19), .out20(I20), .out21(I21), .out22(I22), .out23(I23), .out24(I24),
    .out25(I25), .out26(I26), .out27(I27), .out28(I28), .out29(I29), .out30(I30), .out31(I31), .in(WD),
    .sel(A3));  // open: en
  Multiplexer #(.select(5), .width(32)) multiplexer_1 (
    .in0(O0), .in1(O1), .in2(O2), .in3(O3), .in4(O4), .in5(O5), .in6(O6), .in7(O7), .in8(O8), .in9(O9),
    .in10(O10), .in11(O11), .in12(O12), .in13(O13), .in14(O14), .in15(O15), .in16(O16), .in17(O17),
    .in18(O18), .in19(O19), .in20(O20), .in21(O21), .in22(O22), .in23(O23), .in24(O24), .in25(O25),
    .in26(O26), .in27(O27), .in28(O28), .in29(O29), .in30(O30), .in31(O31), .out(RD2), .sel(A2));  // open: en
  Multiplexer #(.select(5), .width(32)) multiplexer_2 (
    .in0(O0), .in1(O1), .in2(O2), .in3(O3), .in4(O4), .in5(O5), .in6(O6), .in7(O7), .in8(O8), .in9(O9),
    .in10(O10), .in11(O11), .in12(O12), .in13(O13), .in14(O14), .in15(O15), .in16(O16), .in17(O17),
    .in18(O18), .in19(O19), .in20(O20), .in21(O21), .in22(O22), .in23(O23), .in24(O24), .in25(O25),
    .in26(O26), .in27(O27), .in28(O28), .in29(O29), .in30(O30), .in31(O31), .out(RD1), .sel(A1));  // open: en
  Register #(.width(32)) register_1 (.D({32{1'b0}}), .en(we), .Q(O0), .clk(clk), .clr(reset));
  Register #(.width(32)) register_2 (.D(I8), .en(we), .Q(O8), .clk(clk), .clr(reset));
  Register #(.width(32)) register_3 (.D(I16), .en(we), .Q(O16), .clk(clk), .clr(reset));
  Register #(.width(32)) register_4 (.D(I24), .en(we), .Q(O24), .clk(clk), .clr(reset));
  Register #(.width(32)) register_5 (.D(I1), .en(we), .Q(O1), .clk(clk), .clr(reset));
  Register #(.width(32)) register_6 (.D(I9), .en(we), .Q(O9), .clk(clk), .clr(reset));
  Register #(.width(32)) register_7 (.D(I17), .en(we), .Q(O17), .clk(clk), .clr(reset));
  Register #(.width(32)) register_8 (.D(I25), .en(we), .Q(O25), .clk(clk), .clr(reset));
  Register #(.width(32)) register_9 (.D(I2), .en(we), .Q(O2), .clk(clk), .clr(reset));
  Register #(.width(32)) register_10 (.D(I10), .en(we), .Q(O10), .clk(clk), .clr(reset));
  Register #(.width(32)) register_11 (.D(I18), .en(we), .Q(O18), .clk(clk), .clr(reset));
  Register #(.width(32)) register_12 (.D(I26), .en(we), .Q(O26), .clk(clk), .clr(reset));
  Register #(.width(32)) register_13 (.D(I3), .en(we), .Q(O3), .clk(clk), .clr(reset));
  Register #(.width(32)) register_14 (.D(I11), .en(we), .Q(O11), .clk(clk), .clr(reset));
  Register #(.width(32)) register_15 (.D(I19), .en(we), .Q(O19), .clk(clk), .clr(reset));
  Register #(.width(32)) register_16 (.D(I27), .en(we), .Q(O27), .clk(clk), .clr(reset));
  Register #(.width(32)) register_17 (.D(I4), .en(we), .Q(O4), .clk(clk), .clr(reset));
  Register #(.width(32)) register_18 (.D(I12), .en(we), .Q(O12), .clk(clk), .clr(reset));
  Register #(.width(32)) register_19 (.D(I20), .en(we), .Q(O20), .clk(clk), .clr(reset));
  Register #(.width(32)) register_20 (.D(I28), .en(we), .Q(O28), .clk(clk), .clr(reset));
  Register #(.width(32)) register_21 (.D(I5), .en(we), .Q(O5), .clk(clk), .clr(reset));
  Register #(.width(32)) register_22 (.D(I13), .en(we), .Q(O13), .clk(clk), .clr(reset));
  Register #(.width(32)) register_23 (.D(I21), .en(we), .Q(O21), .clk(clk), .clr(reset));
  Register #(.width(32)) register_24 (.D(I29), .en(we), .Q(O29), .clk(clk), .clr(reset));
  Register #(.width(32)) register_25 (.D(I6), .en(we), .Q(O6), .clk(clk), .clr(reset));
  Register #(.width(32)) register_26 (.D(I14), .en(we), .Q(O14), .clk(clk), .clr(reset));
  Register #(.width(32)) register_27 (.D(I22), .en(we), .Q(O22), .clk(clk), .clr(reset));
  Register #(.width(32)) register_28 (.D(I30), .en(we), .Q(O30), .clk(clk), .clr(reset));
  Register #(.width(32)) register_29 (.D(I7), .en(we), .Q(O7), .clk(clk), .clr(reset));
  Register #(.width(32)) register_30 (.D(I15), .en(we), .Q(O15), .clk(clk), .clr(reset));
  Register #(.width(32)) register_31 (.D(I23), .en(we), .Q(O23), .clk(clk), .clr(reset));
  Register #(.width(32)) register_32 (.D(I31), .en(we), .Q(O31), .clk(clk), .clr(reset));

  // Other names for the same wires on the sheet: RST = reset
endmodule

module PC (
  input  [31:0] NPC,
  output [31:0] out_2
);

  wire clk, comparator_1_eq, reset;
  wire [31:0] register_1_q;

  Register #(.width(32)) register_1 (.D(NPC), .en(1'b1), .Q(register_1_q), .clk(clk), .clr(reset));
  Comparator #(.width(32)) comparator_1 (.a(register_1_q), .b({32{1'b0}}), .eq(comparator_1_eq));  // open: gt, lt
  Multiplexer #(.width(32), .enable("false")) multiplexer_1 (
    .in0(register_1_q), .in1(32'h3000), .out(out_2), .sel(comparator_1_eq));
endmodule
